// Logisim project 332 Final project.circ as structural Verilog: 4 circuits, main circuit main
module main (
  input  [3:0] in_1,
  input  [3:0] in_2,
  input  [3:0] in_3,
  input  [3:0] in_4,
  input  [2:0] in_5,
  input  in_6
);

  wire clock_1_out;
  wire [18:0] adder_1_out, register_1_q, undriven;

  Register_part #(.width(19)) register_1 (
    .D(adder_1_out), .Q(register_1_q), .clk(clock_1_out), .clr(in_6));  // open: en
  Clock clock_1 (.out(clock_1_out));
  Adder #(.width(19)) adder_1 (.a(register_1_q), .b(undriven), .out(adder_1_out));  // open: cin, cout
  ROM #(.addrWidth(19), .dataWidth(19)) rom_1 (
    .addr(register_1_q), .data({in_5, in_4, in_3, in_2, in_1}));  // open: sel
  Register register_2 ();  // open: in_1, in_2, out_6, in_4, out_7, in_5, in_3
  RAM #(.addrWidth(19), .dataWidth(19)) ram_1 ();  // open: addr, data, sel, clk, ld, clr
endmodule

module Alu (
  input  cin,
  input  a,
  input  b,
  input  [1:0] in_4,
  output out_5,
  output out_6
);

  wire divider_1_out, nand_1_out, subtractor_1_out, xor_1_out;

  Subtractor #(.width(1)) subtractor_1 (.a(a), .b(b), .out(subtractor_1_out), .bin(cin), .bout(out_6));
  Divider #(.width(1)) divider_1 (.a(a), .b(b), .out(divider_1_out));  // open: upper, rem
  nand nand_1 (nand_1_out, a, b);
  xor xor_1 (xor_1_out, a, b);
  Multiplexer #(.select(2)) multiplexer_1 (
    .in0(subtractor_1_out), .in1(divider_1_out), .in2(nand_1_out), .in3(xor_1_out), .out(out_5), .sel(in_4));  // open: en
endmodule

module Register (
  input  [18:0] in_1,
  input  in_2,
  input  [4:0] in_3,
  input  [4:0] in_4,
  input  [4:0] in_5,
  output [18:0] out_6,
  output [18:0] out_7
);

  wire clock_1_out, demultiplexer_1_out0, demultiplexer_1_out1, demultiplexer_1_out2, demultiplexer_1_out3,
       demultiplexer_1_out4, demultiplexer_1_out5, demultiplexer_1_out6, demultiplexer_1_out7,
       demultiplexer_1_out8, demultiplexer_1_out9, demultiplexer_1_out10, demultiplexer_1_out11,
       demultiplexer_1_out12, demultiplexer_1_out13, demultiplexer_1_out14, demultiplexer_1_out15,
       demultiplexer_1_out16, demultiplexer_1_out17, demultiplexer_1_out18;
  wire [18:0] register_1_q, register_2_q, register_3_q, register_4_q, register_5_q, register_6_q,
       register_7_q, register_8_q, register_9_q, register_10_q, register_11_q, register_12_q, register_13_q,
       register_14_q, register_15_q, register_16_q, register_17_q, register_18_q, register_19_q;

  Demultiplexer #(.select(5)) demultiplexer_1 (
    .out0(demultiplexer_1_out0), .out1(demultiplexer_1_out1), .out2(demultiplexer_1_out2),
    .out3(demultiplexer_1_out3), .out4(demultiplexer_1_out4), .out5(demultiplexer_1_out5),
    .out6(demultiplexer_1_out6), .out7(demultiplexer_1_out7), .out8(demultiplexer_1_out8),
    .out9(demultiplexer_1_out9), .out10(demultiplexer_1_out10), .out11(demultiplexer_1_out11),
    .out12(demultiplexer_1_out12), .out13(demultiplexer_1_out13), .out14(demultiplexer_1_out14),
    .out15(demultiplexer_1_out15), .out16(demultiplexer_1_out16), .out17(demultiplexer_1_out17),
    .out18(demultiplexer_1_out18), .in(in_2), .sel(in_3));  // open: out19, out20, out21, out22, out23, out24, out25, out26, out27, out28, out29, out30, out31, en
  Clock clock_1 (.out(clock_1_out));
  Register_part #(.width(19)) register_1 (
    .D(in_1), .en(demultiplexer_1_out0), .Q(register_1_q), .clk(clock_1_out));  // open: clr
  Register_part #(.width(19)) register_2 (
    .D(in_1), .en(demultiplexer_1_out1), .Q(register_2_q), .clk(clock_1_out));  // open: clr
  Register_part #(.width(19)) register_3 (
    .D(in_1), .en(demultiplexer_1_out2), .Q(register_3_q), .clk(clock_1_out));  // open: clr
  Register_part #(.width(19)) register_4 (
    .D(in_1), .en(demultiplexer_1_out3), .Q(register_4_q), .clk(clock_1_out));  // open: clr
  Register_part #(.width(19)) register_5 (
    .D(in_1), .en(demultiplexer_1_out4), .Q(register_5_q), .clk(clock_1_out));  // open: clr
  Register_part #(.width(19)) register_6 (
    .D(in_1), .en(demultiplexer_1_out5), .Q(register_6_q), .clk(clock_1_out));  // open: clr
  Register_part #(.width(19)) register_7 (
    .D(in_1), .en(demultiplexer_1_out6), .Q(register_7_q), .clk(clock_1_out));  // open: clr
  Register_part #(.width(19)) register_8 (
    .D(in_1), .en(demultiplexer_1_out7), .Q(register_8_q), .clk(clock_1_out));  // open: clr
  Register_part #(.width(19)) register_9 (
    .D(in_1), .en(demultiplexer_1_out8), .Q(register_9_q), .clk(clock_1_out));  // open: clr
  Register_part #(.width(19)) register_10 (
    .D(in_1), .en(demultiplexer_1_out9), .Q(register_10_q), .clk(clock_1_out));  // open: clr
  Register_part #(.width(19)) register_11 (
    .D(in_1), .en(demultiplexer_1_out10), .Q(register_11_q), .clk(clock_1_out));  // open: clr
  Register_part #(.width(19)) register_12 (
    .D(in_1), .en(demultiplexer_1_out11), .Q(register_12_q), .clk(clock_1_out));  // open: clr
  Register_part #(.width(19)) register_13 (
    .D(in_1), .en(demultiplexer_1_out12), .Q(register_13_q), .clk(clock_1_out));  // open: clr
  Register_part #(.width(19)) register_14 (
    .D(in_1), .en(demultiplexer_1_out13), .Q(register_14_q), .clk(clock_1_out));  // open: clr
  Register_part #(.width(19)) register_15 (
    .D(in_1), .en(demultiplexer_1_out14), .Q(register_15_q), .clk(clock_1_out));  // open: clr
  Register_part #(.width(19)) register_16 (
    .D(in_1), .en(demultiplexer_1_out15), .Q(register_16_q), .clk(clock_1_out));  // open: clr
  Register_part #(.width(19)) register_17 (
    .D(in_1), .en(demultiplexer_1_out16), .Q(register_17_q), .clk(clock_1_out));  // open: clr
  Register_part #(.width(19)) register_18 (
    .D(in_1), .en(demultiplexer_1_out17), .Q(register_18_q), .clk(clock_1_out));  // open: clr
  Register_part #(.width(19)) register_19 (
    .D(in_1), .en(demultiplexer_1_out18), .Q(register_19_q), .clk(clock_1_out));  // open: clr
  Multiplexer #(.select(5), .width(19)) multiplexer_1 (
    .in0(register_1_q), .in1(register_2_q), .in2(register_3_q), .in3(register_4_q), .in4(register_5_q),
    .in5(register_6_q), .in6(register_7_q), .in7(register_8_q), .in8(register_9_q), .in9(register_10_q),
    .in10(register_11_q), .in11(register_12_q), .in12(register_13_q), .in13(register_14_q),
    .in14(register_15_q), .in15(register_16_q), .in16(register_17_q), .in17(register_18_q),
    .in18(register_19_q), .out(out_6), .sel(in_4));  // open: in19, in20, in21, in22, in23, in24, in25, in26, in27, in28, in29, in30, in31, en
  Multiplexer #(.select(5), .width(19)) multiplexer_2 (
    .in0(register_1_q), .in1(register_2_q), .in2(register_3_q), .in3(register_4_q), .in4(register_6_q),
    .in5(register_7_q), .in6(register_8_q), .in7(register_10_q), .in8(register_12_q), .in9(register_13_q),
    .in10(register_14_q), .in11(register_16_q), .in12(register_17_q), .in13(register_18_q),
    .in14(register_19_q), .out(out_7), .sel(in_5));  // open: in15, in16, in17, in18, in19, in20, in21, in22, in23, in24, in25, in26, in27, in28, in29, in30, in31, en
endmodule

module alu_2 (
  input  [18:0] in_1,
  input  [18:0] in_2,
  input  cin,
  input  [1:0] opcode,
  output [18:0] out_5,
  output out_6
);

  Alu alu_1 (.out_5(out_5[0]), .out_6(out_6), .a(in_1[18]), .b(in_2[18]), .cin(cin), .in_4(opcode));
  Alu alu_2 (.out_5(out_5[1]), .out_6(out_6), .a(in_1[17]), .b(in_2[17]), .cin(cin), .in_4(opcode));
  Alu alu_3 (.out_5(out_5[2]), .out_6(out_6), .a(in_1[16]), .b(in_2[16]), .cin(cin), .in_4(opcode));
  Alu alu_4 (.out_5(out_5[3]), .out_6(out_6), .a(in_1[15]), .b(in_2[15]), .cin(cin), .in_4(opcode));
  Alu alu_5 (.out_5(out_5[4]), .out_6(out_6), .a(in_1[14]), .b(in_2[14]), .cin(cin), .in_4(opcode));
  Alu alu_6 (.out_5(out_5[5]), .out_6(out_6), .a(in_1[13]), .b(in_2[13]), .cin(cin), .in_4(opcode));
  Alu alu_7 (.out_5(out_5[6]), .out_6(out_6), .a(in_1[12]), .b(in_2[12]), .cin(cin), .in_4(opcode));
  Alu alu_8 (.out_5(out_5[7]), .out_6(out_6), .a(in_1[11]), .b(in_2[11]), .cin(cin), .in_4(opcode));
  Alu alu_9 (.out_5(out_5[8]), .out_6(out_6), .a(in_1[10]), .b(in_2[10]), .cin(cin), .in_4(opcode));
  Alu alu_10 (.out_5(out_5[9]), .out_6(out_6), .a(in_1[9]), .b(in_2[9]), .cin(cin), .in_4(opcode));
  Alu alu_11 (.out_5(out_5[10]), .out_6(out_6), .a(in_1[8]), .b(in_2[8]), .cin(cin), .in_4(opcode));
  Alu alu_12 (.out_5(out_5[11]), .out_6(out_6), .a(in_1[7]), .b(in_2[7]), .cin(cin), .in_4(opcode));
  Alu alu_13 (.out_5(out_5[12]), .out_6(out_6), .a(in_1[6]), .b(in_2[6]), .cin(cin), .in_4(opcode));
  Alu alu_14 (.out_5(out_5[13]), .out_6(out_6), .a(in_1[5]), .b(in_2[5]), .cin(cin), .in_4(opcode));
  Alu alu_15 (.out_5(out_5[14]), .out_6(out_6), .a(in_1[4]), .b(in_2[4]), .cin(cin), .in_4(opcode));
  Alu alu_16 (.out_5(out_5[15]), .out_6(out_6), .a(in_1[3]), .b(in_2[3]), .cin(cin), .in_4(opcode));
  Alu alu_17 (.out_5(out_5[16]), .out_6(out_6), .a(in_1[2]), .b(in_2[2]), .cin(cin), .in_4(opcode));
  Alu alu_18 (.out_5(out_5[17]), .out_6(out_6), .a(in_1[1]), .b(in_2[1]), .cin(cin), .in_4(opcode));
  Alu alu_19 (.out_5(out_5[18]), .out_6(out_6), .a(in_1[0]), .b(in_2[0]), .cin(cin), .in_4(opcode));
endmodule
